// Logisim project Projeto.circ as structural Verilog: 7 circuits, main circuit main
module somador_1bit (
  input  cin,
  input  A,
  input  B,
  output S,
  output cout
);

  wire and_1_out, and_2_out, xor_1_out;

  xor xor_1 (xor_1_out, A, B);
  and and_1 (and_1_out, A, B);
  xor xor_2 (S, cin, xor_1_out);
  and and_2 (and_2_out, cin, xor_1_out);
  or or_1 (cout, and_2_out, and_1_out);
endmodule

module main (
  input  [1:0] xy,
  input  [3:0] B,
  input  [3:0] A,
  output [3:0] S,
  output [3:0] S_2,
  output [3:0] S_3,
  output out_7,
  output out_8,
  output [3:0] S_4
);

  somador_4bit somador_4bit_1 (.A(A), .Overflow(out_7), .B(B), .S(S_4));
  subtrator_4bit subtrator_4bit_1 (.A(A), .Overflow(out_8), .B(B), .S(S_3));
  Rot_Esq rot_esq_1 (.abcd(A), .xy(xy), .ABCD_2(S));
  Rot_Dir rot_dir_1 (.abcd(A), .xy(xy), .ABCD_2(S_2));
endmodule

module somador_4bit (
  input  [3:0] B,
  input  [3:0] A,
  output Overflow,
  output [3:0] S
);

  wire somador_1bit_2_cout, somador_1bit_3_cout, somador_1bit_4_cout;

  somador_1bit somador_1bit_1 (.cin(somador_1bit_2_cout), .A(A[3]), .B(B[3]), .S(S[3]), .cout(Overflow));
  somador_1bit somador_1bit_2 (.cin(somador_1bit_3_cout), .A(A[2]), .B(B[2]), .S(S[2]), .cout(somador_1bit_2_cout));
  somador_1bit somador_1bit_3 (.cin(somador_1bit_4_cout), .A(A[1]), .B(B[1]), .S(S[1]), .cout(somador_1bit_3_cout));
  somador_1bit somador_1bit_4 (.cin(1'b0), .A(A[0]), .B(B[0]), .S(S[0]), .cout(somador_1bit_4_cout));
endmodule

module subtrator_1bit (
  input  A,
  input  B,
  input  C,
  output S,
  output Vai_1
);

  wire and_1_out, and_2_out, or_1_out, xor_1_out;

  xor xor_1 (xor_1_out, C, B);
  or or_1 (or_1_out, C, B);
  xor xor_2 (S, xor_1_out, A);
  and and_1 (and_1_out, or_1_out, ~A);  // AND_Gate
  and and_2 (and_2_out, C, B);
  or or_2 (Vai_1, and_1_out, and_2_out);
endmodule

module subtrator_4bit (
  input  [3:0] B,
  input  [3:0] A,
  output Overflow,
  output [3:0] S
);

  wire subtrator_1bit_2_vai_1, subtrator_1bit_3_vai_1, subtrator_1bit_4_vai_1;

  subtrator_1bit subtrator_1bit_1 (.S(S[3]), .Vai_1(Overflow), .A(A[3]), .B(B[3]), .C(subtrator_1bit_2_vai_1));
  subtrator_1bit subtrator_1bit_2 (
    .S(S[2]), .Vai_1(subtrator_1bit_2_vai_1), .A(A[2]), .B(B[2]), .C(subtrator_1bit_3_vai_1));
  subtrator_1bit subtrator_1bit_3 (
    .S(S[1]), .Vai_1(subtrator_1bit_3_vai_1), .A(A[1]), .B(B[1]), .C(subtrator_1bit_4_vai_1));
  subtrator_1bit subtrator_1bit_4 (.S(S[0]), .Vai_1(subtrator_1bit_4_vai_1), .A(A[0]), .B(B[0]), .C(1'b0));
endmodule

module Rot_Esq (
  input  [3:0] abcd,
  input  [1:0] xy,
  output [3:0] ABCD_2
);

  wire and_1_out, and_2_out, and_3_out, and_4_out, and_5_out, and_6_out, and_7_out, and_8_out, and_9_out;

  and and_1 (and_1_out, ~xy[1], ~xy[0], abcd[3]);  // AND_Gate
  and and_2 (and_2_out, ~xy[1], xy[0], abcd[2]);  // AND_Gate
  and and_3 (and_3_out, xy[1], ~xy[0], abcd[1]);  // AND_Gate
  and and_4 (and_4_out, xy[1], xy[0], abcd[0]);
  and and_5 (and_5_out, ~xy[1], ~xy[0], abcd[2]);  // AND_Gate
  and and_6 (and_6_out, ~xy[1], xy[0], abcd[1]);  // AND_Gate
  and and_7 (and_7_out, xy[1], ~xy[0], abcd[0]);  // AND_Gate
  and and_8 (and_8_out, ~xy[1], ~xy[0], abcd[1]);  // AND_Gate
  and and_9 (and_9_out, ~xy[1], xy[0], abcd[0]);  // AND_Gate
  and and_10 (ABCD_2[0], ~xy[1], ~xy[0], abcd[0]);  // AND_Gate
  or or_1 (ABCD_2[3], and_1_out, and_2_out, and_3_out, and_4_out);
  or or_2 (ABCD_2[2], and_5_out, and_6_out, and_7_out);
  or or_3 (ABCD_2[1], and_8_out, and_9_out);
endmodule

module Rot_Dir (
  input  [3:0] abcd,
  input  [1:0] xy,
  output [3:0] ABCD_2
);

  wire and_1_out, and_2_out, and_3_out, and_4_out, and_5_out, and_6_out, and_7_out, and_8_out, and_9_out;

  and and_1 (and_1_out, ~xy[1], ~xy[0], abcd[0]);  // AND_Gate
  and and_2 (and_2_out, ~xy[1], xy[0], abcd[1]);  // AND_Gate
  and and_3 (and_3_out, xy[1], ~xy[0], abcd[2]);  // AND_Gate
  and and_4 (and_4_out, xy[1], xy[0], abcd[3]);
  and and_5 (and_5_out, ~xy[1], ~xy[0], abcd[1]);  // AND_Gate
  and and_6 (and_6_out, ~xy[1], xy[0], abcd[2]);  // AND_Gate
  and and_7 (and_7_out, xy[1], ~xy[0], abcd[3]);  // AND_Gate
  and and_8 (and_8_out, ~xy[1], ~xy[0], abcd[2]);  // AND_Gate
  and and_9 (and_9_out, ~xy[1], xy[0], abcd[3]);  // AND_Gate
  and and_10 (ABCD_2[3], ~xy[1], ~xy[0], abcd[3]);  // AND_Gate
  or or_1 (ABCD_2[0], and_1_out, and_2_out, and_3_out, and_4_out);
  or or_2 (ABCD_2[1], and_5_out, and_6_out, and_7_out);
  or or_3 (ABCD_2[2], and_8_out, and_9_out);
endmodule
